// Logisim project regfile.circ as structural Verilog: 1 circuit, main circuit regfile
module regfile (
  input  [4:0] rs1,
  input  [4:0] rs2,
  input  [4:0] rd,
  input  [31:0] Write_Data,
  input  RegWEn,
  input  clk,
  output [31:0] ra,
  output [31:0] sp,
  output [31:0] t0,
  output [31:0] t1,
  output [31:0] t2,
  output [31:0] s0,
  output [31:0] s1,
  output [31:0] a0,
  output [31:0] Read_Data_1,
  output [31:0] Read_Data_2
);

  wire write_en1, write_en2, write_en3, write_en4, write_en5, write_en6, write_en7, write_en8, write_en9,
       write_en10, write_en11, write_en12, write_en13, write_en14, write_en15, write_en16, write_en17,
       write_en18, write_en19, write_en20, write_en21, write_en22, write_en23, write_en24, write_en25,
       write_en26, write_en27, write_en28, write_en29, write_en30, write_en31;
  wire [31:0] x0_out, x1_in, x2_in, x3, x3_in, x4, x4_in, x5_in, x6_in, x7_in, x8_in, x9_in, x10_in, x11,
       x11_in, x12, x12_in, x13, x13_in, x14, x14_in, x15, x15_in, x16, x16_in, x17, x17_in, x18, x18_in,
       x19, x19_in, x20, x20_in, x21, x21_in, x22, x22_in, x23, x23_in, x24, x24_in, x25, x25_in, x26,
       x26_in, x27, x27_in, x28, x28_in, x29, x29_in, x30, x30_in, x31, x31_in;

  Multiplexer #(.enable("false"), .select(5), .width(32)) multiplexer_1 (
    .in0(x0_out), .in1(ra), .in2(sp), .in3(x3), .in4(x4), .in5(t0), .in6(t1), .in7(t2), .in8(s0), .in9(s1),
    .in10(a0), .in11(x11), .in12(x12), .in13(x13), .in14(x14), .in15(x15), .in16(x16), .in17(x17),
    .in18(x18), .in19(x19), .in20(x20), .in21(x21), .in22(x22), .in23(x23), .in24(x24), .in25(x25),
    .in26(x26), .in27(x27), .in28(x28), .in29(x29), .in30(x30), .in31(x31), .out(Read_Data_1), .sel(rs1));
  Multiplexer #(.enable("false"), .select(5), .width(32)) multiplexer_2 (
    .in0(x0_out), .in1(ra), .in2(sp), .in3(x3), .in4(x4), .in5(t0), .in6(t1), .in7(t2), .in8(s0), .in9(s1),
    .in10(a0), .in11(x11), .in12(x12), .in13(x13), .in14(x14), .in15(x15), .in16(x16), .in17(x17),
    .in18(x18), .in19(x19), .in20(x20), .in21(x21), .in22(x22), .in23(x23), .in24(x24), .in25(x25),
    .in26(x26), .in27(x27), .in28(x28), .in29(x29), .in30(x30), .in31(x31), .out(Read_Data_2), .sel(rs2));
  Register #(.width(32)) x_0 (.D({32{1'b0}}), .en(1'b1), .clk(clk), .Q(x0_out));  // open: clr
  Register #(.width(32)) x_1 (.D(x1_in), .en(write_en1), .clk(clk), .Q(ra));  // open: clr
  Register #(.width(32)) x_2 (.D(x2_in), .en(write_en2), .clk(clk), .Q(sp));  // open: clr
  Register #(.width(32)) x_5 (.D(x5_in), .en(write_en5), .clk(clk), .Q(t0));  // open: clr
  Register #(.width(32)) x_6 (.D(x6_in), .en(write_en6), .clk(clk), .Q(t1));  // open: clr
  Register #(.width(32)) x_7 (.D(x7_in), .en(write_en7), .clk(clk), .Q(t2));  // open: clr
  Register #(.width(32)) x_8 (.D(x8_in), .en(write_en8), .clk(clk), .Q(s0));  // open: clr
  Register #(.width(32)) x_9 (.D(x9_in), .en(write_en9), .clk(clk), .Q(s1));  // open: clr
  Register #(.width(32)) x_10 (.D(x10_in), .en(write_en10), .clk(clk), .Q(a0));  // open: clr
  Register #(.width(32)) x_3 (.D(x3_in), .en(write_en3), .clk(clk), .Q(x3));  // open: clr
  Register #(.width(32)) x_4 (.D(x4_in), .en(write_en4), .clk(clk), .Q(x4));  // open: clr
  Register #(.width(32)) x_11 (.D(x11_in), .en(write_en11), .clk(clk), .Q(x11));  // open: clr
  Register #(.width(32)) x_12 (.D(x12_in), .en(write_en12), .clk(clk), .Q(x12));  // open: clr
  Register #(.width(32)) x_13 (.D(x13_in), .en(write_en13), .clk(clk), .Q(x13));  // open: clr
  Register #(.width(32)) x_14 (.D(x14_in), .en(write_en14), .clk(clk), .Q(x14));  // open: clr
  Register #(.width(32)) x_15 (.D(x15_in), .en(write_en15), .clk(clk), .Q(x15));  // open: clr
  Register #(.width(32)) x_16 (.D(x16_in), .en(write_en16), .clk(clk), .Q(x16));  // open: clr
  Register #(.width(32)) x_17 (.D(x17_in), .en(write_en17), .clk(clk), .Q(x17));  // open: clr
  Register #(.width(32)) x_18 (.D(x18_in), .en(write_en18), .clk(clk), .Q(x18));  // open: clr
  Register #(.width(32)) x_19 (.D(x19_in), .en(write_en19), .clk(clk), .Q(x19));  // open: clr
  Register #(.width(32)) x_20 (.D(x20_in), .en(write_en20), .clk(clk), .Q(x20));  // open: clr
  Register #(.width(32)) x_21 (.D(x21_in), .en(write_en21), .clk(clk), .Q(x21));  // open: clr
  Register #(.width(32)) x_22 (.D(x22_in), .en(write_en22), .clk(clk), .Q(x22));  // open: clr
  Register #(.width(32)) x_23 (.D(x23_in), .en(write_en23), .clk(clk), .Q(x23));  // open: clr
  Register #(.width(32)) x_24 (.D(x24_in), .en(write_en24), .clk(clk), .Q(x24));  // open: clr
  Register #(.width(32)) x_25 (.D(x25_in), .en(write_en25), .clk(clk), .Q(x25));  // open: clr
  Register #(.width(32)) x_26 (.D(x26_in), .en(write_en26), .clk(clk), .Q(x26));  // open: clr
  Register #(.width(32)) x_27 (.D(x27_in), .en(write_en27), .clk(clk), .Q(x27));  // open: clr
  Register #(.width(32)) x_28 (.D(x28_in), .en(write_en28), .clk(clk), .Q(x28));  // open: clr
  Register #(.width(32)) x_29 (.D(x29_in), .en(write_en29), .clk(clk), .Q(x29));  // open: clr
  Register #(.width(32)) x_30 (.D(x30_in), .en(write_en30), .clk(clk), .Q(x30));  // open: clr
  Register #(.width(32)) x_31 (.D(x31_in), .en(write_en31), .clk(clk), .Q(x31));  // open: clr
  Demultiplexer #(.enable("false"), .select(5), .width(32)) demultiplexer_1 (
    .out1(x1_in), .out2(x2_in), .out3(x3_in), .out4(x4_in), .out5(x5_in), .out6(x6_in), .out7(x7_in),
    .out8(x8_in), .out9(x9_in), .out10(x10_in), .out11(x11_in), .out12(x12_in), .out13(x13_in),
    .out14(x14_in), .out15(x15_in), .out16(x16_in), .out17(x17_in), .out18(x18_in), .out20(x20_in),
    .out21(x21_in), .out22(x22_in), .out23(x23_in), .out24(x24_in), .out25(x25_in), .out26(x26_in),
    .out27(x27_in), .out28(x28_in), .out29(x29_in), .out30(x30_in), .out31(x31_in), .in(Write_Data), .sel(rd));  // open: out0, out19
  Demultiplexer #(.enable("false"), .select(5)) demultiplexer_2 (
    .out1(write_en1), .out2(write_en2), .out3(write_en3), .out4(write_en4), .out5(write_en5),
    .out6(write_en6), .out7(write_en7), .out8(write_en8), .out9(write_en9), .out10(write_en10),
    .out11(write_en11), .out12(write_en12), .out13(write_en13), .out14(write_en14), .out15(write_en15),
    .out16(write_en16), .out17(write_en17), .out18(write_en18), .out19(write_en19), .out20(write_en20),
    .out21(write_en21), .out22(write_en22), .out23(write_en23), .out24(write_en24), .out25(write_en25),
    .out26(write_en26), .out27(write_en27), .out28(write_en28), .out29(write_en29), .out30(write_en30),
    .out31(write_en31), .in(RegWEn), .sel(rd));  // open: out0

  // Other names for the same wires on the sheet: read_data1[31:0] = Read_Data_1; read_data2[31:0] = Read_Data_2;
  //   read_reg1[4:0] = rs1; read_reg2[4:0] = rs2; write_en = RegWEn; write_reg[4:0] = rd

  // Notes on the sheet:
  //   INPUTS to your circuit
  //   DON'T CHANGE THE LOCATIONS OF THE INPUTS AND OUTPUTS!
  //   These are DEBUG/TEST outputs from your circuit.
  //   OUTPUTS from your circuit
endmodule
