// Logisim project alu-comprehensive.circ as structural Verilog: 1 circuit, main circuit main
module main (
  output [7:0] Test,
  output [31:0] Result,
  output halt,
  output [3:0] ALU_Sel,
  output [31:0] Input_A,
  output [31:0] Input_B
);

  wire clock_1_out;
  wire [7:0] adder_1_out;

  Clock clock_1 (.out(clock_1_out));
  Adder adder_1 (.a(8'h1), .b(Test), .out(adder_1_out));  // open: cin, cout
  Register register_1 (.D(adder_1_out), .clk(clock_1_out), .Q(Test));  // open: en, clr
  ROM #(.dataWidth(32)) rom_1 (.addr(Test), .data(Input_A));
  Comparator comparator_1 (.a(Test), .b(8'h18), .eq(halt));  // open: gt, lt
  // Probe on Input_B
  ROM #(.dataWidth(32)) rom_2 (.addr(Test), .data(Input_B));
  // Probe on ALU_Sel
  // Probe on Input_A
  alu alu_1 (.Result(Result), .A(Input_A), .B(Input_B), .ALUSel(ALU_Sel));
  ROM #(.dataWidth(4)) rom_3 (.addr(Test), .data(ALU_Sel));

  // Notes on the sheet:
  //   contents of rom_1 (hex, n*v repeats v):
  //   ffffffff 5 ffff0000 10101010 ffff0000 10101010 ffff0000 10101010 6*f234567f ffffabcd 5 ffffabcd
  //   ffffffff ffffabcd ffffffff 4  ffff0007 88dcd902 f819cd72
  //   Your ALU must fit here!
  //   contents of rom_2 (hex, n*v repeats v):
  //   ffffbeef aa abcd0000 1010 abcd0000 1010 abcd0000 1010 9 fe9 9 fe9 9 fe9 5 ffffabcd ffffffff ffffabcd
  //   ffffffff ffffabcd 3 ffff0009 1 2
  //   There should be no red or blue wires, and the result should not be all X's
  //   contents of rom_3 (hex, n*v repeats v):
  //   0 0 1 1 2 2 3 3 4 4 5 5 6 6 7 7 a a b b c c d d
endmodule
